// Logisim project elevator controller.circ as structural Verilog: 4 circuits, main circuit contoller
module contoller (
  input  Go2Floor,
  input  Go1Floor,
  input  Go0Floor,
  input  Call2Floor,
  input  Call1Floor,
  input  Call0Floor,
  output Go2Floor_2,
  output Go1Floor_2,
  output Go0Floor_2,
  output Call2Floor_2,
  output Call1Floor_2,
  output Call0Floor_2
);

  wire clock_1_out;

  Clock clock_1 (.out(clock_1_out));
  D_Flip_Flop Go2Floorff (.Q(Go2Floor_2), .preset(Go2Floor), .reset(clock_1_out));  // open: clk, D, Qn, en
  D_Flip_Flop Go1Floorff (.Q(Go1Floor_2), .preset(Go1Floor), .reset(clock_1_out));  // open: clk, D, Qn, en
  D_Flip_Flop Go0Floorff (.Q(Go0Floor_2), .preset(Go0Floor), .reset(clock_1_out));  // open: clk, D, Qn, en
  D_Flip_Flop Call2Floorff (.Q(Call2Floor_2), .preset(Call2Floor), .reset(clock_1_out));  // open: clk, D, Qn, en
  D_Flip_Flop Call1Floorff (.Q(Call1Floor_2), .preset(Call1Floor), .reset(clock_1_out));  // open: clk, D, Qn, en
  D_Flip_Flop Call0Floorff (.Q(Call0Floor_2), .preset(Call0Floor), .reset(clock_1_out));  // open: clk, D, Qn, en

  // Notes on the sheet:
  //   Clock
endmodule

module controller2 (
  input  _0Floor,
  input  _1Floor,
  input  _2Florr,
  input  Call0Floor,
  input  Call1Floor,
  input  Call2Floor,
  input  Go0Floor,
  input  Go1Floor,
  input  Go2Floor,
  output _0Floor_2,
  output _1Floor_2,
  output _2Floor,
  output Availablity,
  output Door,
  output Up,
  output Down
);

  wire and_1_out, and_2_out, and_3_out, and_4_out, and_5_out, and_6_out, and_7_out, and_8_out, and_9_out,
       and_10_out, and_11_out, and_12_out, and_13_out, and_14_out, and_15_out, and_16_out, and_17_out,
       and_18_out, and_19_out, and_20_out, and_21_out, and_22_out, and_23_out, and_24_out, and_25_out,
       and_26_out, and_27_out, and_28_out, and_29_out, and_30_out, and_31_out, not_1_out, not_2_out,
       not_3_out, not_4_out, not_5_out, not_6_out, not_7_out, not_8_out, not_9_out, not_10_out, not_11_out,
       not_12_out, not_13_out, not_14_out, not_15_out, not_16_out, not_17_out, not_18_out, not_19_out,
       not_20_out, not_21_out, not_22_out, not_23_out, not_24_out, not_25_out, not_26_out, not_27_out,
       not_28_out, not_29_out, not_30_out, not_31_out, not_32_out, not_33_out, not_34_out, not_35_out,
       not_36_out, not_37_out, not_38_out;

  not not_1 (not_1_out, Call1Floor);
  not not_2 (not_2_out, Call2Floor);
  not not_3 (not_3_out, Go1Floor);
  not not_4 (not_4_out, Go2Floor);
  not not_5 (not_5_out, Call0Floor);
  not not_6 (not_6_out, Call2Floor);
  not not_7 (not_7_out, Go0Floor);
  not not_8 (not_8_out, Go2Floor);
  not not_9 (not_9_out, _0Floor);
  not not_10 (not_10_out, _0Floor);
  not not_11 (not_11_out, Call0Floor);
  not not_12 (not_12_out, Call1Floor);
  not not_13 (not_13_out, Go0Floor);
  not not_14 (not_14_out, Go1Floor);
  not not_15 (not_15_out, _2Florr);
  not not_16 (not_16_out, _1Floor);
  not not_17 (not_17_out, _0Floor);
  not not_18 (not_18_out, _2Florr);
  not not_19 (not_19_out, _1Floor);
  not not_20 (not_20_out, _0Floor);
  not not_21 (not_21_out, _2Florr);
  not not_22 (not_22_out, _1Floor);
  not not_23 (not_23_out, _0Floor);
  not not_24 (not_24_out, _0Floor);
  not not_25 (not_25_out, _1Floor);
  not not_26 (not_26_out, _2Florr);
  not not_27 (not_27_out, _2Florr);
  not not_28 (not_28_out, _1Floor);
  not not_29 (not_29_out, _2Florr);
  not not_30 (not_30_out, _2Florr);
  not not_31 (not_31_out, _1Floor);
  not not_32 (not_32_out, _2Florr);
  and and_1 (and_1_out, _0Floor, not_1_out, not_2_out, not_3_out, not_4_out);
  and and_2 (and_2_out, _1Floor, Go0Floor);
  and and_3 (and_3_out, _1Floor, Call0Floor);
  and and_4 (and_4_out, _2Florr, Go0Floor);
  and and_5 (and_5_out, _2Florr, Call0Floor);
  and and_6 (and_6_out, _1Floor, not_5_out, not_6_out, not_7_out, not_8_out);
  and and_7 (and_7_out, _0Floor, Go2Floor);
  and and_8 (and_8_out, _0Floor, Call2Floor);
  and and_9 (and_9_out, not_9_out, Go2Floor);
  and and_10 (and_10_out, not_10_out, Call2Floor);
  and and_11 (and_11_out, _2Florr, not_11_out, not_12_out, not_13_out, not_14_out);
  and and_12 (and_12_out, not_15_out, Go2Floor);
  and and_13 (and_13_out, not_16_out, Go1Floor);
  and and_14 (and_14_out, not_17_out, Go0Floor);
  and and_15 (and_15_out, not_18_out, Call2Floor);
  and and_16 (and_16_out, not_19_out, Call1Floor);
  and and_17 (and_17_out, not_20_out, Call0Floor);
  and and_18 (and_18_out, not_21_out, Go2Floor);
  and and_19 (and_19_out, not_22_out, Go1Floor);
  and and_20 (and_20_out, not_23_out, Go0Floor);
  and and_21 (and_21_out, not_24_out, Call0Floor);
  and and_22 (and_22_out, not_25_out, Call1Floor);
  and and_23 (and_23_out, not_26_out, Call2Floor);
  and and_24 (and_24_out, not_27_out, Go2Floor);
  and and_25 (and_25_out, not_28_out, not_29_out, Go1Floor);
  and and_26 (and_26_out, not_30_out, Call2Floor);
  and and_27 (and_27_out, not_31_out, not_32_out, Call1Floor);
  not not_33 (not_33_out, _1Floor);
  not not_34 (not_34_out, _0Floor);
  not not_35 (not_35_out, _1Floor);
  not not_36 (not_36_out, _0Floor);
  not not_37 (not_37_out, _0Floor);
  not not_38 (not_38_out, _0Floor);
  or or_1 (_0Floor_2, and_1_out, and_2_out, and_3_out);
  or or_2 (_1Floor_2, Go1Floor, Call1Floor, and_4_out, and_5_out, and_6_out, and_7_out, and_8_out);
  or or_3 (_2Floor, and_9_out, and_10_out, and_11_out);
  or or_4 (Availablity, and_12_out, and_13_out, and_14_out, and_15_out, and_16_out, and_17_out);
  or or_5 (Up, and_24_out, and_25_out, and_26_out, and_27_out);
  or or_6 (Door, and_18_out, and_19_out, and_20_out, and_21_out, and_22_out, and_23_out);
  and and_28 (and_28_out, Go1Floor, not_33_out, not_34_out);
  and and_29 (and_29_out, Call1Floor, not_35_out, not_36_out);
  and and_30 (and_30_out, Call0Floor, not_37_out);
  and and_31 (and_31_out, Go0Floor, not_38_out);
  or or_7 (Down, and_28_out, and_29_out, and_30_out, and_31_out);
endmodule

module _7segment (
  input  kat0,
  input  kat1,
  input  kat2,
  output a,
  output b,
  output c,
  output d,
  output e,
  output f,
  output g,
  output nokta
);

  wire and_1_out, and_2_out, and_3_out, and_4_out, and_5_out, and_6_out, and_7_out, and_8_out, and_9_out,
       and_10_out, and_11_out, not_1_out, not_2_out, not_3_out, not_4_out, not_5_out, not_6_out, not_7_out,
       not_8_out, not_9_out, not_10_out, not_11_out, not_12_out, not_13_out, not_14_out, not_15_out,
       not_16_out, not_17_out, not_18_out, not_19_out, not_20_out, not_21_out, not_22_out, not_23_out,
       not_24_out, not_25_out, not_26_out;

  not not_1 (not_1_out, kat0);
  not not_2 (not_2_out, kat1);
  not not_3 (not_3_out, kat1);
  not not_4 (not_4_out, kat2);
  not not_5 (not_5_out, kat0);
  not not_6 (not_6_out, kat1);
  not not_7 (not_7_out, kat0);
  not not_8 (not_8_out, kat2);
  not not_9 (not_9_out, kat1);
  not not_10 (not_10_out, kat2);
  not not_11 (not_11_out, kat0);
  not not_12 (not_12_out, kat2);
  not not_13 (not_13_out, kat1);
  not not_14 (not_14_out, kat2);
  not not_15 (not_15_out, kat0);
  not not_16 (not_16_out, kat1);
  not not_17 (not_17_out, kat1);
  not not_18 (not_18_out, kat2);
  not not_19 (not_19_out, kat0);
  not not_20 (not_20_out, kat1);
  not not_21 (not_21_out, kat1);
  not not_22 (not_22_out, kat2);
  not not_23 (not_23_out, kat1);
  not not_24 (not_24_out, kat2);
  not not_25 (not_25_out, kat0);
  not not_26 (not_26_out, kat1);
  and and_1 (and_1_out, not_1_out, not_2_out, kat2);
  and and_2 (and_2_out, kat0, not_3_out, not_4_out);
  and and_3 (and_3_out, not_5_out, not_6_out, kat2);
  and and_4 (and_4_out, not_7_out, kat1, not_8_out);
  and and_5 (and_5_out, kat0, not_9_out, not_10_out);
  and and_6 (and_6_out, not_11_out, kat1, not_12_out);
  and and_7 (and_7_out, kat0, not_13_out, not_14_out);
  and and_8 (and_8_out, not_15_out, not_16_out, kat2);
  and and_9 (and_9_out, kat0, not_17_out, not_18_out);
  and and_10 (and_10_out, not_19_out, not_20_out, kat2);
  and and_11 (and_11_out, kat0, not_21_out, not_22_out);
  and and_12 (f, kat0, not_23_out, not_24_out);
  and and_13 (g, not_25_out, not_26_out, kat2);
  or or_1 (a, and_1_out, and_2_out);
  or or_2 (b, and_3_out, and_4_out, and_5_out);
  or or_3 (c, and_6_out, and_7_out);
  or or_4 (d, and_8_out, and_9_out);
  or or_5 (e, and_10_out, and_11_out);

  assign nokta = 1'b0;
endmodule

module elevator_main (
  input  Outside,
  input  Inside
);

  wire _0Floor_q, _1Floor_q, _2Floor_q, call0floor1_q, call0floor2_q, call1floor1_q, call2floor1_q,
       call2floor2_q, CALL_to_1st_out, CALL_to_2nd_out, CALL_to_floor_out, Clock_out, contolller2_1_p10,
       contolller2_1_p11, contolller2_1_p12, contolller2_1_p13, contolller2_1_p14, contolller2_1_p15,
       contolller2_1_p16, controller_1_p7, controller_1_p8, controller_1_p9, controller_1_p10,
       controller_1_p11, controller_1_p12, decoder_1_out0, decoder_1_out1, decoder_2_out0, decoder_2_out1,
       go0floor1_q, go0floor2_q, go1floor1_q, go2floor1_q, go2floor2_q, GO_1st_out, Go_2nd_out, GO_floor_out,
       n7segment_1_p4, n7segment_1_p5, n7segment_1_p6, n7segment_1_p7, n7segment_1_p8, n7segment_1_p9,
       n7segment_1_p10, n7segment_1_p11, not_1_out, or_1_out, or_2_out, or_3_out, or_4_out;

  or or_1 (or_1_out, call0floor2_q, call0floor1_q);
  or or_2 (or_2_out, call2floor2_q, call2floor1_q);
  Clock Clock (.out(Clock_out));
  D_Flip_Flop _0Floor (.clk(Clock_out), .D(contolller2_1_p10), .Q(_0Floor_q));  // open: Qn, preset, en, reset
  D_Flip_Flop _1Floor (.clk(Clock_out), .D(contolller2_1_p11), .Q(_1Floor_q));  // open: Qn, preset, en, reset
  D_Flip_Flop _2Floor (.clk(Clock_out), .D(contolller2_1_p12), .Q(_2Floor_q));  // open: Qn, preset, en, reset
  D_Flip_Flop call0floor2 (.clk(Clock_out), .D(call0floor1_q), .Q(call0floor2_q));  // open: Qn, preset, en, reset
  D_Flip_Flop call0floor1 (.clk(Clock_out), .D(controller_1_p12), .Q(call0floor1_q));  // open: Qn, preset, en, reset
  D_Flip_Flop call2floor2 (.clk(Clock_out), .D(call2floor1_q), .Q(call2floor2_q));  // open: Qn, preset, en, reset
  D_Flip_Flop call2floor1 (.clk(Clock_out), .D(controller_1_p10), .Q(call2floor1_q));  // open: Qn, preset, en, reset
  D_Flip_Flop go1floor1 (.clk(Clock_out), .D(controller_1_p8), .Q(go1floor1_q));  // open: Qn, preset, en, reset
  D_Flip_Flop call1floor1 (.clk(Clock_out), .D(controller_1_p11), .Q(call1floor1_q));  // open: Qn, preset, en, reset
  D_Flip_Flop go0floor2 (.clk(Clock_out), .D(go0floor1_q), .Q(go0floor2_q));  // open: Qn, preset, en, reset
  or or_3 (or_3_out, go0floor2_q, go0floor1_q);
  D_Flip_Flop go0floor1 (.clk(Clock_out), .D(controller_1_p9), .Q(go0floor1_q));  // open: Qn, preset, en, reset
  D_Flip_Flop go2floor2 (.clk(Clock_out), .D(go2floor1_q), .Q(go2floor2_q));  // open: Qn, preset, en, reset
  or or_4 (or_4_out, go2floor2_q, go2floor1_q);
  D_Flip_Flop go2floor1 (.clk(Clock_out), .D(controller_1_p7), .Q(go2floor1_q));  // open: Qn, preset, en, reset
  // contolller2 contolller2_1: pin names not known; wires that end beside it: _0Floor_q, _1Floor_q, _2Floor_q, or_1_out, call1floor1_q, or_2_out, or_3_out, go1floor1_q, or_4_out, contolller2_1_p10, contolller2_1_p11, contolller2_1_p12, contolller2_1_p13, contolller2_1_p14, contolller2_1_p15, contolller2_1_p16
  LED _0 (.in(contolller2_1_p10));
  Decoder #(.enable("false")) decoder_1 (.out0(decoder_1_out0), .out1(decoder_1_out1), .sel(contolller2_1_p14));
  LED _2 (.in(contolller2_1_p12));
  LED _1 (.in(contolller2_1_p11));
  not not_1 (not_1_out, contolller2_1_p13);
  Decoder #(.enable("false")) decoder_2 (.out0(decoder_2_out0), .out1(decoder_2_out1), .sel(contolller2_1_p13));
  // abc_7segment 7segment_1: pin names not known; wires that end beside it: contolller2_1_p10, contolller2_1_p11, contolller2_1_p12, n7segment_1_p4, n7segment_1_p5, n7segment_1_p6, n7segment_1_p7, n7segment_1_p8, n7segment_1_p9, n7segment_1_p10, n7segment_1_p11
  _7_Segment_Display u_7_segment_display_1 (
    .g(n7segment_1_p10), .f(n7segment_1_p9), .a(n7segment_1_p4), .b(n7segment_1_p5), .e(n7segment_1_p8),
    .d(n7segment_1_p7), .c(n7segment_1_p6), .dp(n7segment_1_p11));
  LED Up (.in(contolller2_1_p15));
  LED Down (.in(contolller2_1_p16));
  LED Ready (.in(not_1_out));
  LED Door_Closed (.in(decoder_1_out1));
  Button CALL_to_2nd (.out(CALL_to_2nd_out));
  Button CALL_to_1st (.out(CALL_to_1st_out));
  Button CALL_to_floor (.out(CALL_to_floor_out));
  LED Door_Open (.in(decoder_1_out0));
  LED Busy (.in(decoder_2_out1));
  LED Usable (.in(decoder_2_out0));
  Button Go_2nd (.out(Go_2nd_out));
  Button GO_1st (.out(GO_1st_out));
  Button GO_floor (.out(GO_floor_out));
  // controller controller_1: pin names not known; wires that end beside it: Go_2nd_out, GO_1st_out, GO_floor_out, CALL_to_2nd_out, CALL_to_1st_out, CALL_to_floor_out, controller_1_p7, controller_1_p8, controller_1_p9, controller_1_p10, controller_1_p11, controller_1_p12

  // Notes on the sheet:
  //   current status
  //   Decoders
  //   Floor Display
endmodule
